# Fritzing sketch ouchi_sensor (saved by Fritzing 0.9.0b)
breadboards: 1

parts:
  U1 = Spark Core (v1.0)
  R1 = Resistor [tolerance=±10% resistance=1k package=THT]
  RHT1 = Humidity and Temperature Sensor RHT03

nets:
  3V3: U1.A2, U1.3V3, R1.Pin_0, RHT1.Vcc
  N1: U1.A3, U1.A6
  N2: U1.A5, U1.VIN
  N3: U1.GND, RHT1.GND_2
  N4: U1.D2, R1.Pin_1, RHT1.Data-signal

custom parts:
  Spark Core (v1.0): The Spark Core is a tiny Wi-Fi development board that makes it easy to create internet-connected hardware. The Core is all you need to get started; power it over USB and in minutes you'll be controlling LEDs, switches and motors and collecting data from sensors over the internet! It has 8 digital I/O pins, 8 analog I/O pins, 8 PWM pins; UART (Serial), SPI, I2C, and JTAG peripherals available.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
